// Logisim project Test1.circ as structural Verilog: 1 circuit, main circuit main
module main (
  input  in_1,
  input  in_2,
  output out_3
);

  wire and_1_out, not_1_out, not_2_out, xor_1_out;

  not not_1 (not_1_out, in_1);
  not not_2 (not_2_out, in_2);
  and and_1 (and_1_out, not_1_out, not_2_out);
  xor xor_1 (xor_1_out, in_1, in_2);
  xor xor_2 (out_3, and_1_out, xor_1_out);
endmodule
