// Logisim project Test3.circ as structural Verilog: 1 circuit, main circuit main
module main (
  input  a,
  input  s,
  input  b,
  output out_4
);

  wire and_1_out, and_2_out, not_1_out, not_2_out;

  not not_1 (not_1_out, s);
  and and_1 (and_1_out, a, not_1_out);
  and and_2 (and_2_out, s, b);
  not not_2 (not_2_out, and_1_out);
  and and_3 (out_4, not_2_out, and_2_out);
endmodule
