// Logisim project Test 2.circ as structural Verilog: 1 circuit, main circuit main
module main (
  input  in_1,
  input  in_2,
  output out_3
);

  wire and_1_out, nand_1_out, not_1_out;

  not not_1 (not_1_out, in_2);
  buf and_1 (and_1_out, not_1_out);  // AND_Gate
  not nand_1 (nand_1_out, in_1);  // NAND_Gate
  nor nor_1 (out_3, and_1_out, nand_1_out);
endmodule
