// Logisim project Test5.circ as structural Verilog: 1 circuit, main circuit main
module main (
  input  in_1,
  input  in_2,
  input  in_3,
  output out_4
);

  wire and_1_out, not_1_out, xor_1_out;

  xor xor_1 (xor_1_out, in_2, in_1);
  and and_1 (and_1_out, in_1, in_2, in_3);
  not not_1 (not_1_out, xor_1_out);
  nor nor_1 (out_4, and_1_out, not_1_out);
endmodule
